// Logisim project Proyecto Logica.circ as structural Verilog: 1 circuit, main circuit main
module main (
  input  A,
  input  B,
  input  C,
  input  D
);

  wire a_out, b_out, c_out, d_out, e_out, f_out, g_out, not_1_out, not_2_out, not_3_out, not_4_out, or_1_out,
       or_2_out, or_3_out, or_4_out, or_5_out, or_6_out, or_7_out, or_8_out, or_9_out, or_10_out, or_11_out,
       or_12_out, or_13_out, or_14_out, or_15_out, or_16_out, or_17_out, or_18_out, or_19_out, or_20_out,
       or_21_out, or_22_out, or_23_out, or_24_out, or_25_out;

  not not_1 (not_1_out, A);
  not not_2 (not_2_out, B);
  not not_3 (not_3_out, C);
  not not_4 (not_4_out, D);
  or or_1 (or_1_out, A, not_2_out, C, D);
  or or_2 (or_2_out, A, B, C, not_4_out);
  or or_3 (or_3_out, not_1_out, not_2_out, C, not_4_out);
  or or_4 (or_4_out, not_1_out, B, not_3_out, not_4_out);
  or or_5 (or_5_out, A, not_2_out, C, not_4_out);
  or or_6 (or_6_out, not_1_out, not_2_out, D);
  or or_7 (or_7_out, not_1_out, not_3_out, not_4_out);
  or or_8 (or_8_out, not_2_out, not_3_out, D);
  or or_9 (or_9_out, A, B, not_3_out, D);
  or or_10 (or_10_out, not_1_out, not_2_out, not_3_out);
  or or_11 (or_11_out, not_1_out, not_2_out, D);
  or or_12 (or_12_out, A, not_2_out, C, D);
  or or_13 (or_13_out, A, B, C, not_4_out);
  or or_14 (or_14_out, not_1_out, B, not_3_out, D);
  or or_15 (or_15_out, not_2_out, not_3_out, not_4_out);
  or or_16 (or_16_out, A, not_2_out, C);
  or or_17 (or_17_out, B, C, not_4_out);
  or or_18 (or_18_out, A, not_4_out);
  or or_19 (or_19_out, not_1_out, not_2_out, C, not_4_out);
  or or_20 (or_20_out, A, B, not_4_out);
  or or_21 (or_21_out, A, B, not_3_out);
  or or_22 (or_22_out, A, not_3_out, not_4_out);
  or or_23 (or_23_out, not_1_out, not_2_out, C, D);
  or or_24 (or_24_out, A, not_2_out, not_3_out, not_4_out);
  or or_25 (or_25_out, A, B, C);
  and u_a (a_out, or_1_out, or_2_out, or_3_out, or_4_out);
  and e (e_out, or_16_out, or_17_out, or_18_out);
  and f (f_out, or_19_out, or_20_out, or_21_out, or_22_out);
  and u_b (b_out, or_5_out, or_6_out, or_7_out, or_8_out);
  and u_c (c_out, or_9_out, or_10_out, or_11_out);
  and u_d (d_out, or_12_out, or_13_out, or_14_out, or_15_out);
  and g (g_out, or_23_out, or_24_out, or_25_out);
  _7_Segment_Display u_7_segment_display_1 (
    .g(g_out), .f(f_out), .a(a_out), .b(b_out), .e(e_out), .d(d_out), .c(c_out));  // open: dp
endmodule
